# Fritzing sketch led tester v2 (saved by Fritzing 0.9.2b)
circuit board: 2.44962cm x 2.18259cm
breadboards: 1

parts:
  5mm = LED - 5mm [color="Red (633nm)" package="5 mm [THT]"]
  6x6x5mm_4_Pins_SMD_Tact_Switch = Pushbutton [package="[THT]"]
  LED1_0805 = smd LED [color="Blue (525nm)" package="0805 [SMD]"]
  0603 = smd LED [color="Red (633nm)" package="0603 [SMD]"]
  0805 = smd LED [color="Red (633nm)" package="0805 [SMD]"]
  1206 = Blue smd LED [package="1206 [SMD]"]
  68_ohm1_0805 = Resistor [tolerance=±5% resistance=68 package="0805 [SMD]"]
  68_ohm_0805 = Resistor [tolerance=±5% resistance=68 package="0805 [SMD]"]
  CR2032_(20mm_SMD) = Battery Holders [package=battcon_12mm_pth]

nets:
  N1: 5mm.anode, 0603.cathode, 0805.cathode, 1206.cathode_+, 68_ohm1_0805.Pin_1
  GND: 5mm.cathode, LED1_0805.cathode, 0603.anode, 0805.anode, 1206.anode_-, CR2032_(20mm_SMD).-
  N2: 6x6x5mm_4_Pins_SMD_Tact_Switch.Pin_1, 6x6x5mm_4_Pins_SMD_Tact_Switch.Pin_2, 68_ohm1_0805.Pin_0, CR2032_(20mm_SMD).+
  N3: 6x6x5mm_4_Pins_SMD_Tact_Switch.Pin_3, 6x6x5mm_4_Pins_SMD_Tact_Switch.Pin_4, 68_ohm_0805.Pin_0
  N4: LED1_0805.anode, 68_ohm_0805.Pin_1

notes:
  BATT
  LED TEST
  +
  -
  CR2100-3V
  -----
  LED Tester v0.3

custom parts:
  Red LED - 5mm: A generic red LED (~1.8V)
  Blue smd LED: A generic blue LED (~1.8V)
